# Fritzing sketch lcd_wiring_gnd (saved by Fritzing 0.9.3b)
stripboards: 1

parts:
  LCD1 = LCD screen
  R1 = Resistor [tolerance=±5% resistance=1k package=THT]
  R2 = Resistor [tolerance=±5% resistance=2k package=THT]

nets:
  N1: LCD1.VSS, LCD1.R/W, R1.Pin_0, R2.Pin_1
  N2: LCD1.V0, R2.Pin_0
  N3: LCD1.LED-, R1.Pin_1

notes:
  K
  V0
  1K Ohms or Trimpot
  RW
  VSS
  GND (Rpi)
  2K Ohms or Trimpot
