# Fritzing sketch lcd_wiring_gpio (saved by Fritzing 0.9.3b)

parts:
  LCD1 = LCD screen
  Raspberry_Pi_1 = Raspberry Pi 3 [part_number=RPI-3-V1.2]

nets:
  N1: LCD1.RS, Raspberry_Pi_1.GIPO7
  N2: LCD1.E, Raspberry_Pi_1.GIPO8
  N3: LCD1.DB4, Raspberry_Pi_1.GIPO25
  N4: LCD1.DB5, Raspberry_Pi_1.GIPO24
  N5: LCD1.DB6, Raspberry_Pi_1.GIPO23
  N6: LCD1.DB7, Raspberry_Pi_1.GIPO18

notes:
  RS:7
  EN:8
  D4:25
  D6:23
  D5:24
  D7:18
